# Fritzing sketch impulse_connection (saved by Fritzing 0.9.2b)

parts:
  J2 = female pin header, 4 pins [form="♀ (female)"]
  J3 = female pin header, 4 pins [form="♀ (female)"]
  ESP8266_module = ESP8266 WiFi Module [part_number=ESP8266]
  LED1 = LED - 5mm [color="Red (633nm)" package="5 mm [THT]"]
  R1 = Resistor [tolerance=±5% resistance=10k package=THT]
  IMPULSE_SENSOR_PINS = male pin header, 2 pins [form="♂ (male)"]
  Power_plug = Power plug
  S1 = Toggle Switch [package=THT]

nets:
  N1: J2.pin1, ESP8266_module.GND, IMPULSE_SENSOR_PINS.pin1, S1.COM
  N2: J2.pin2, ESP8266_module.GPIO_2, R1.Pin_1, IMPULSE_SENSOR_PINS.pin2
  N3: J2.pin3, ESP8266_module.GPIO_0, LED1.cathode
  VCC: J3.pin4, ESP8266_module.VCC, ESP8266_module.CH_PD, LED1.anode, R1.Pin_0, Power_plug.VCC
  N4: Power_plug.GND, S1.L1

notes:
  IMPULSE SENSOR:
  VCC +
  GND -

custom parts:
  ESP8266 WiFi Module: Generic WiFi Module based on the ESP8266 with onboard PCB antenna and UART communications
