# Fritzing sketch rs485_connection (saved by Fritzing 0.9.2b)

parts:
  J2 = female pin header, 4 pins [form="♀ (female)"]
  J3 = female pin header, 4 pins [form="♀ (female)"]
  ESP8266_module = ESP8266 WiFi Module [part_number=ESP8266]
  LED1 = LED - 5mm [color="Red (633nm)" package="5 mm [THT]"]
  Power_plug = Power plug
  RS485_SENSOR_PINS_(OUTPUT) = double row male pin header, 4 pins [form="♂ (male)"]
  RS485_SENSOR_PINS_(INPUT) = double row male pin header, 4 pins [form="♂ (male)"]  # not connected
  S1 = Toggle Switch [package=THT]

nets:
  N1: J2.pin1, ESP8266_module.GND, S1.COM
  N2: J2.pin2, ESP8266_module.GPIO_2, RS485_SENSOR_PINS_(OUTPUT).pin2, RS485_SENSOR_PINS_(OUTPUT).pin3
  N3: J2.pin3, ESP8266_module.GPIO_0, LED1.cathode
  N4: J2.pin4, ESP8266_module.RXD, RS485_SENSOR_PINS_(OUTPUT).pin1
  N5: J3.pin1, ESP8266_module.TXD, RS485_SENSOR_PINS_(OUTPUT).pin4
  VCC: J3.pin4, ESP8266_module.VCC, ESP8266_module.CH_PD, LED1.anode, Power_plug.VCC
  N6: Power_plug.GND, S1.L1

notes:
  LC Electronics RS485 Converter (MAX485-based):
  input:
  A - A
  B - B
  VCC - 3.3V
  GND - GND
  output:
  DI - TX1
  RO - RX0
  DE,RE - GPIO_2 (ESP8266)

custom parts:
  ESP8266 WiFi Module: Generic WiFi Module based on the ESP8266 with onboard PCB antenna and UART communications
